# Fritzing sketch smokematic (saved by Fritzing 0.8.7b)
circuit board: 8.46667cm x 5.64444cm

parts:
  BeagleBone1 = BeagleBone Black
  C1 = Ceramic Capacitor [capacitance=0.1µF voltage=50V package="0603 [SMD, multilayer]"]
  R2 = Resistor [tolerance=±5% resistance=1k package=THT]
  R3 = Resistor [tolerance=±5% resistance=1k package=THT]
  Q2 = TIP120 Hi-Current Darlington Transistor
  Q3 = TIP120 Hi-Current Darlington Transistor
  VALVE1 = Plastic Solenoid Valve
  J1 = Power Jack [package=power_jack_slot]
  M1 = DC Motor
  C2 = Ceramic Capacitor [capacitance=0.1µF voltage=50V package="0603 [SMD, multilayer]"]
  D3 = Rectifier Diode [part_number=1N4001 package="300 mil [THT]"]
  D4 = Rectifier Diode [part_number=1N4001 package="300 mil [THT]"]
  R4 = Resistor [tolerance=±1% resistance=10k package=THT]
  R5 = Temperature Sensor (Thermistor) [thermistor_type=NTC package=THT]
  R6 = Resistor [tolerance=±1% resistance=10k package=THT]
  R7 = Temperature Sensor (Thermistor) [thermistor_type=NTC package=THT]

nets:
  N1: BeagleBone1.no_name_yet#14, R3.Pin_0
  N2: BeagleBone1.no_name_yet#32, R4.Pin_0, R6.Pin_0
  N3: BeagleBone1.no_name_yet#34, R5.pin_0, R7.pin_0
  N4: BeagleBone1.no_name_yet#39, R4.Pin_1, R5.pin_1
  N5: BeagleBone1.no_name_yet#40, R6.Pin_1, R7.pin_1
  N6: BeagleBone1.no_name_yet#46, Q2.EMITTER
  N7: BeagleBone1.no_name_yet#101, J1.GND
  N8: BeagleBone1.no_name_yet#114, R2.Pin_0
  N9: BeagleBone1.no_name_yet#146, Q3.EMITTER
  N10: C1.0, Q3.COLLECTOR, VALVE1.no_name_yet#2, D4.anode
  N11: C1.1, VALVE1.no_name_yet#1, J1.PWR, M1.pin_1, C2.1, D3.cathode, D4.cathode
  N12: R2.Pin_1, Q3.BASE
  N13: R3.Pin_1, Q2.BASE
  N14: Q2.COLLECTOR, M1.pin_2, C2.0, D3.anode

notes:
  Food Probe
  Pit Probe

custom parts:
  BeagleBone Black: BeagleBone Black rev. A5B
